# Fritzing sketch sketch (saved by Fritzing 0.9.4)

parts:
  Компонент1 = Arduino Due (Rev2b)
  M1 = Niren can bus module [package=THT]
  OLED_I2C1 = OLED 128x64 I2C Monochrome Display
  J2 = Basic Servo

nets:
  N1: Компонент1.D20/SDA3, OLED_I2C1.SDA
  N2: Компонент1.D21/SCL3, OLED_I2C1.SCK
  N3: Компонент1.IOREF, OLED_I2C1.VDD
  5V: Компонент1.5V, M1.pin1, J2.vcc
  GND: Компонент1.GND, M1.pin2, OLED_I2C1.GND, J2.gnd
  N4: Компонент1.D9_PWM, J2.pulse
  N5: Компонент1.D10_PWM/SS0, M1.pin3
  N6: Компонент1.D11_PWM, M1.pin7
  N7: M1.pin8, M1.pin9

notes:
  The green wire is connected to the second pin of the servo potentiometer

custom parts:
  Niren can bus module: Niren can bus module availabe on ebay and others. Pcb view assumes that you unsolder the 7 pin header and resolder it on the bottom of the module to connect to the pcb. The two jumpers and the can bus connector remain on the top of the board and don't appear in pcb view.

// code stored in the sketch: Active_Grille_Shutter.ino
/**
   https://github.com/adafruit/Adafruit-GFX-Library
   Commit: 0752d4bd4f35407684c1123e618368719b95ec22

   https://github.com/adafruit/Adafruit_SSD1306
   Commit: d62796bbe860e046265ba1251a0bf89b15e3481e

   https://github.com/Seeed-Studio/CAN_BUS_Shield
   Commit: edaba2d87efc597770079d6ed63f09aa246eba29
*/
#include <Adafruit_GFX.h>
#include <Adafruit_SSD1306.h>
#include <Servo.h>
#include <SPI.h>
#include <mcp_can.h>

// Print messages to Serial
#define DEBUG_MODE true

// GPIO the display is attached to
#define pinCanCs        10
#define pinCanInt       11
#define interruptCan    0
const int SPI_CS_PIN = pinCanCs;
const int INT_PIN = pinCanInt;

// Change this values if you are using a custom font
#define DEFAULT_SYMBOL_WIDTH  6
#define DEFAULT_SYMBOL_HEIGHT 8

// OLED display width and height, in pixels
#define SCREEN_WIDTH  128
#define SCREEN_HEIGHT 64

// GPIO the display is attached to
#define pinDisplaySDA 20
#define pinDisplaySCL 21

// GPIO the servo is attached to
#define pinServo        9
#define pinServoAnalog  A2

// Config for servo
#define servoDelay        8
#define servoDiagDelay    30
#define servoMinUs        720  // 0
#define servoMaxUs        2400 // 180
#define servoMaxAttempts  3

// Min and max degree for rotation servo
#define servoDegreeMin  45  // 0
#define servoDegreeMax  105 // 170

// Min and max analog values
#define servoAnalogMin  320 // 195
#define servoAnalogMax  485 // 645

// Possible difference between values
#define servoAnalogDegreesDiff  5
#define servoAnalogAnalogDiff   50

// Progress Bar
#define textSize                2
#define progressBarTextSize     2
#define progressBarBorder       1   // px
#define progressBarMarginOuter  13  // px
#define progressBarHeightOuter  13  // px
#define progressBarLengthOuter  (SCREEN_WIDTH - progressBarMarginOuter * 2)
#define progressBarMarginInner  progressBarMarginOuter + progressBarBorder
#define progressBarHeightInner  progressBarHeightOuter - progressBarBorder * 2
#define progressBarLengthInner  progressBarLengthOuter - (progressBarBorder * 2)

Adafruit_SSD1306 display(SCREEN_WIDTH, SCREEN_HEIGHT, &Wire);
Servo servo;
MCP_CAN CAN(pinCanCs);

bool isDataUpdated = false;

float cvtfTemp;
float engineTemp;
float engineTemp2;
float carSpeed;
float carSpeed2;
int shutterDegree;

int newDegree = servoDegreeMin;
int analogDegree;
unsigned long timer;

volatile bool hasNewMessage = false;
unsigned char len = 0;
unsigned char buf[8];

void drawProgressBar(int y, int progress, int margin = 13, int height = 13);
bool writeServo(int degree, bool isDiagnostics = false);

void setup() {
  if (DEBUG_MODE) {
    Serial.begin(115200);
  }
  println("[INIT] Debug mode is enabled");
  println("[INIT] Starting...");

  initDisplay();
  println("--------------");
  initCan();
  println("--------------");
  initServo();
  println("--------------");
  servoDiagnostics();

  println("[INIT] Initialization is complete");

  renderAllData();
}

void loop() {
  while (CAN_MSGAVAIL == CAN.checkReceive()) {
    CAN.readMsgBuf(&len, buf);
    canMessageProcessing(CAN.getCanId(), buf);
  }

  if (isDataUpdated) {
    isDataUpdated = false;
    openCloseShutters();
    renderAllData();
  }
}

// Open or close grille shutters
void openCloseShutters() {
  float temp = getEngineTemp();
  float speed = getSpeed();
  bool openShutters = true;

  if (temp <= 75) {
    openShutters = false;
  }

  if (speed > 130) {
    openShutters = (temp > 90);
  }

  print("[INFO] Shutters must be ");
  print(String(openShutters ? servoDegreeMin : servoDegreeMax));
  print(" ");
  print("(" + String(openShutters ? "open" : "close") + ")");
  println("");

  int degreeNeedle = openShutters ? servoDegreeMin : servoDegreeMax;
  if (!isServoRotated(degreeNeedle)) {
    writeServo(degreeNeedle);
  }
}

void renderAllData() {
  display.setTextSize(textSize);
  display.clearDisplay();

  renderEngineTemp();
  renderCarSpeed();
  renderProgressBar();

  display.display();
}

void renderEngineTemp() {
  display.setCursor(0, 0);
  //display.println(String(getEngineTemp(), 1) + " oC");
  display.println(String(getEngineTemp(), 1) + "|" + String(getEngineTemp2(), 0));
}

void renderCarSpeed() {
  display.setCursor(0, 16);
  //display.println(String(getSpeed(), 1) + " km/h");
  display.println(String(getSpeed(), 1) + "|" + String(getSpeed2(), 1));
}

void renderProgressBar() {
  int shutterDegrees = getShutterDegree();
  //String text = String(shutterDegrees);
  String text = String(getCvtfTemp(), 1);
  int progress = map(shutterDegrees, servoDegreeMin, servoDegreeMax, 0, progressBarLengthInner);
  int y = constrain(51, 0, SCREEN_HEIGHT);
  int x = (SCREEN_WIDTH - text.length() * DEFAULT_SYMBOL_WIDTH * progressBarTextSize) / 2;

  display.setTextSize(progressBarTextSize);
  display.setCursor(x, y - DEFAULT_SYMBOL_HEIGHT * progressBarTextSize);
  display.println(text);

  display.drawRect(
    progressBarMarginOuter,
    y,
    progressBarLengthOuter,
    progressBarHeightOuter,
    HIGH
  );
  display.fillRect(
    progressBarMarginInner,
    y + progressBarBorder,
    progress ? : progressBarLengthInner,
    progressBarHeightInner,
    progress ? HIGH : LOW
  );
  display.display();
}

float getCvtfTemp() {
  return cvtfTemp;
}

float getEngineTemp() {
  return engineTemp;
}

float getEngineTemp2() {
  return engineTemp2;
}

float getSpeed() {
  return carSpeed;
}

float getSpeed2() {
  return carSpeed2;
}

int getShutterDegree() {
  return shutterDegree;
}

// CAN message processing
void canMessageProcessing(unsigned long messageId, byte* messageData) {
  String id = String(messageId, HEX);

  // Engine temp 1
  if (id == "324") {
    float engineTempOld = getEngineTemp();

    engineTemp = messageData[0] - 40.0;

    if (engineTempOld != engineTemp) {
      isDataUpdated = true;

      println("EngineTemp: " + String(getEngineTemp()));
    }
  }
  // Engine temp 2
  else if (id == "396") {
    float engineTemp2Old = getEngineTemp2();

    engineTemp2 = (float) messageData[2];

    if (engineTemp2Old != engineTemp2) {
      isDataUpdated = true;

      println("EngineTemp2: " + String(getEngineTemp2()));
    }
  }
  // Speeds (general)
  else if (id == "158") {
    float carSpeedOld = getSpeed();
    float carSpeed2Old = getSpeed2();

    carSpeed = (messageData[0] * 256 + messageData[1]) / 100.0;
    carSpeed2 = (messageData[4] * 256 + messageData[5]) / 100.0;

    if (carSpeedOld != carSpeed || carSpeed2Old != carSpeed2) {
      isDataUpdated = true;

      println("Speed: " + String(getSpeed()));
      println("Speed2: " + String(getSpeed2()));
    }
  }
  // CVTF temp
  else if (id == "510") {
    float cvtfTempOld = getCvtfTemp();

    cvtfTemp = messageData[5] - 40.0;

    if (cvtfTempOld != cvtfTemp) {
      isDataUpdated = true;

      println("CvtfTemp: " + String(getCvtfTemp()));
    }
  }
}

// Returns analog degree for servo
int getAnalogDegree() {
  int analogVal = analogRead(pinServoAnalog);
  analogVal = constrain(analogVal, servoAnalogMin, servoAnalogMax);
  analogDegree = map(analogVal, servoAnalogMin, servoAnalogMax, servoDegreeMin, servoDegreeMax);

  return analogDegree;
}

// It returns the status of whether the servo turned
bool isServoRotated(int degreeNeedle) {
  bool rotated = false;

  // Check by analog value
  int analogVal = analogRead(pinServoAnalog);
  int checkMinAnalog = servoAnalogMin - servoAnalogAnalogDiff;
  int checkMaxAnalog = servoAnalogMax + servoAnalogAnalogDiff;
  rotated = analogVal > checkMinAnalog && analogVal < checkMaxAnalog;

  print("[INFO] Analog: ");
  print(String(analogVal));
  println(" | Diff min: " + String(checkMinAnalog) + " | Diff max: " + String(checkMaxAnalog));

  // Check by digital value
  if (rotated) {
    int degreeAnalog = getAnalogDegree();
    int checkMin = degreeNeedle - servoAnalogDegreesDiff;
    int checkMax = degreeNeedle + servoAnalogDegreesDiff;
    rotated = degreeAnalog > checkMin && degreeAnalog < checkMax;

    print("[INFO] Digital: ");
    print(String(degreeAnalog) + "/" + String(degreeNeedle) + " (Analog/Digital)");
    println(" | Diff min: " + String(checkMin) + " | Diff max: " + String(checkMax));
  }

  println(rotated ? "[OK] Servo is rotated!" : "[FAIL] Servo is not rotated!");

  display.println("Servo: " + String(analogVal) + "|" + String(degreeNeedle));
  display.display();

  return rotated;
}

// Rotate servo
bool writeServo(int degree, bool isDiagnostics) {
  int start = getAnalogDegree();
  int end = degree;
  int position;

  if (start > end) {
    for (position = start; position >= end; position--)
    {
      servo.write(position);
      delay(isDiagnostics ? servoDiagDelay : servoDelay);
    }
  } else {
    for (position = start; position <= end; position++)
    {
      servo.write(position);
      delay(isDiagnostics ? servoDiagDelay : servoDelay);
    }
  }

  delay(300);

  shutterDegree = constrain(getAnalogDegree(), servoDegreeMin, servoDegreeMax);

  return isServoRotated(degree);
}

// Display initialization
void initDisplay() {
  if (!display.begin(SSD1306_SWITCHCAPVCC, 0x3C)) {
    println("[FAIL] SSD1306 allocation failed");
    for (;;);
  }
  println("[OK] SSD1306 allocation successful");

  display.clearDisplay();
  display.setTextColor(HIGH, LOW);
  display.display();

  println("[INIT] Display initialized");
}

// CAN bus initialization
void initCan() {
  //pinMode(pinCanInt, INPUT);
  while (CAN_OK != CAN.begin(CAN_500KBPS, MCP_8MHz)) {
    println("[FAIL] CAN BUS module init fail");
    println("[FAIL] Init CAN BUS module again");
    delay(100);
  }
  //CAN.setMode(MODE_NORMAL);

  println("[INIT] CAN initialized");

  // Hardware filters
  CAN.init_Mask(0, 0, 0x158);
  CAN.init_Mask(1, 0, 0x510);
  CAN.init_Filt(0, 0, 0x158);
  CAN.init_Filt(1, 0, 0x324);
  CAN.init_Filt(2, 0, 0x396);
  CAN.init_Filt(3, 0, 0x510);

  println("[INIT] CAN filters added");
}

// Servo initialization
void initServo() {
  pinMode(pinServoAnalog, INPUT);

  servo.attach(
    pinServo,
    servoMinUs,
    servoMaxUs
  );

  if (servo.attached()) {
    println("[INIT] Servo attached");
  }

  writeServo(newDegree);
}

// Diagnostics for servo
void servoDiagnostics() {
  display.setCursor(0, 0);
  display.println("Servo diag: start");
  display.display();

  println("[INIT] Servo diagnostics: start");

  bool diagStatus = true;
  diagStatus = writeServo(servoDegreeMax, true);

  //display.println("Servo diag #1: " + String(diagStatus ? "OK" : "FAIL"));
  //display.display();

  print(diagStatus ? "[OK]" : "[FAIL]");
  println(" Servo diagnostics #1 (to " + String(servoDegreeMax) + "°)");

  if (diagStatus) {
    diagStatus = writeServo(servoDegreeMin, true);
  }

  //display.println("Servo diag #2: " + String(diagStatus ? "OK" : "FAIL"));
  //display.display();

  print(diagStatus ? "[OK]" : "[FAIL]");
  println(" Servo diagnostics #2 (to " + String(servoDegreeMin) + "°)");

  if (diagStatus) {
    diagStatus = writeServo(servoDegreeMax, true);
  }

  //display.println("Servo diag #3: " + String(diagStatus ? "OK" : "FAIL"));
  //display.display();

  print(diagStatus ? "[OK]" : "[FAIL]");
  println(" Servo diagnostics #3 (to " + String(servoDegreeMax) + "°)");

  if (diagStatus) {
    diagStatus = writeServo(servoDegreeMin, true);
  }

  //display.println("Servo diag #4: " + String(diagStatus ? "OK" : "FAIL"));
  //display.display();

  print(diagStatus ? "[OK]" : "[FAIL]");
  println(" Servo diagnostics #4 (to " + String(servoDegreeMin) + "°)");

  if (!diagStatus) {
    while (true) {
      if (millis() - timer >= 3000) {
        timer = millis();

        display.println("");
        display.println("Life Is Pain");
        display.println("Shit happens...");
        display.display();

        println("[FAIL] Servo diagnostics: Shit happens...");
      }
    }
  }

  display.println("");
  display.println("Success!");
  display.display();

  println("[INIT] Servo diagnostics: success");
}

// Print message to Serial
void print(String message) {
  if (DEBUG_MODE) {
    Serial.print(message);
  }
}

// Print message to Serial
void println(String message) {
  if (DEBUG_MODE) {
    Serial.println(message);
  }
}

// code stored in the sketch: CAN_Decoder.ino
/**
   https://github.com/autowp/arduino-canhacker
   Commit: 7bcbf0a751f198edbee1844c7b6020c252c8c08d

   https://github.com/autowp/arduino-mcp2515
   Commit: cdc0141ee734f47f54628b1ac8acaafa9120511b
*/
#include <can.h>
#include <mcp2515.h>

#include <CanHacker.h>
#include <CanHackerLineReader.h>
#include <lib.h>

#include <SPI.h>

// Uncomment when debugging is needed
//#define DEBUG_ENABLED

#define dataSerial SerialUSB
#ifdef DEBUG_ENABLED
#define debugSerial Serial1
#endif

const int SPI_CS_PIN = 10;
const int INT_PIN = 11;

CanHackerLineReader *lineReader = NULL;
CanHacker *canHacker = NULL;

void setup() {
#ifdef DEBUG_ENABLED
  debugSerial.begin(115200);
  while (!debugSerial);
#endif

  dataSerial.begin(115200);
  while (!dataSerial);

  SPI.begin();

  Stream *interfaceStream = &dataSerial;
#ifdef DEBUG_ENABLED
  Stream *debugStream = &debugSerial;
#else
  Stream *debugStream = NULL;
#endif

  canHacker = new CanHacker(interfaceStream, debugStream, SPI_CS_PIN);
  canHacker->setClock(MCP_8MHZ); // MCP_8MHZ, MCP_16MHZ or MCP_20MHZ
  lineReader = new CanHackerLineReader(canHacker);

  pinMode(INT_PIN, INPUT);
}

void loop() {
  CanHacker::ERROR error;

  if (digitalRead(INT_PIN) == LOW) {
    error = canHacker->processInterrupt();
    handleError(error);
  }

  error = lineReader->process();
  handleError(error);
}

void handleError(const CanHacker::ERROR error) {

  switch (error) {
    case CanHacker::ERROR_OK:
    case CanHacker::ERROR_UNKNOWN_COMMAND:
    case CanHacker::ERROR_NOT_CONNECTED:
    case CanHacker::ERROR_MCP2515_ERRIF:
    case CanHacker::ERROR_INVALID_COMMAND:
      return;

    default:
      break;
  }

#ifdef DEBUG_ENABLED
  debugSerial.print("Failure (code ");
  debugSerial.print((int)error);
  debugSerial.println(")");
#endif

  digitalWrite(SPI_CS_PIN, HIGH);
  pinMode(LED_BUILTIN, OUTPUT);

  while (1) {
    int c = (int)error;
    for (int i = 0; i < c; i++) {
      digitalWrite(LED_BUILTIN, HIGH);
      delay(500);
      digitalWrite(LED_BUILTIN, LOW);
      delay(500);
    }

    delay(2000);
  };
}

// code stored in the sketch: sketch.ino
/**
   https://github.com/adafruit/Adafruit-GFX-Library
   Commit: 0752d4bd4f35407684c1123e618368719b95ec22

   https://github.com/adafruit/Adafruit_SSD1306
   Commit: d62796bbe860e046265ba1251a0bf89b15e3481e

   https://github.com/Seeed-Studio/CAN_BUS_Shield
   Commit: edaba2d87efc597770079d6ed63f09aa246eba29
*/
#include <Adafruit_GFX.h>
#include <Adafruit_SSD1306.h>
#include <Servo.h>
#include <SPI.h>
#include <mcp_can.h>

// Print messages to Serial
#define DEBUG_MODE true

// GPIO the display is attached to
#define pinCanCs        10
#define pinCanInt       11
#define interruptCan    0
const int SPI_CS_PIN = pinCanCs;
const int INT_PIN = pinCanInt;

// Change this values if you are using a custom font
#define DEFAULT_SYMBOL_WIDTH  6
#define DEFAULT_SYMBOL_HEIGHT 8

// OLED display width and height, in pixels
#define SCREEN_WIDTH  128
#define SCREEN_HEIGHT 64

// GPIO the display is attached to
#define pinDisplaySDA 20
#define pinDisplaySCL 21

// GPIO the servo is attached to
#define pinServo        9
#define pinServoAnalog  A2

// Config for servo
#define servoDelay        8
#define servoDiagDelay    30
#define servoMinUs        720  // 0
#define servoMaxUs        2400 // 180
#define servoMaxAttempts  3

// Min and max degree for rotation servo
#define servoDegreeMin  45  // 0
#define servoDegreeMax  105 // 170

// Min and max analog values
#define servoAnalogMin  320 // 195
#define servoAnalogMax  485 // 645

// Possible difference between values
#define servoAnalogDegreesDiff  5
#define servoAnalogAnalogDiff   50

// Progress Bar
#define textSize                2
#define progressBarTextSize     2
#define progressBarBorder       1   // px
#define progressBarMarginOuter  13  // px
#define progressBarHeightOuter  13  // px
#define progressBarLengthOuter  (SCREEN_WIDTH - progressBarMarginOuter * 2)
#define progressBarMarginInner  progressBarMarginOuter + progressBarBorder
#define progressBarHeightInner  progressBarHeightOuter - progressBarBorder * 2
#define progressBarLengthInner  progressBarLengthOuter - (progressBarBorder * 2)

Adafruit_SSD1306 display(SCREEN_WIDTH, SCREEN_HEIGHT, &Wire);
Servo servo;
MCP_CAN CAN(pinCanCs);

bool isDataUpdated = false;

float cvtfTemp;
float engineTemp;
float engineTemp2;
float carSpeed;
float carSpeed2;
int shutterDegree;

int newDegree = servoDegreeMin;
int analogDegree;
unsigned long timer;

volatile bool hasNewMessage = false;
unsigned char len = 0;
unsigned char buf[8];

void drawProgressBar(int y, int progress, int margin = 13, int height = 13);
bool writeServo(int degree, bool isDiagnostics = false);

void setup() {
  if (DEBUG_MODE) {
    Serial.begin(115200);
  }
  println("[INIT] Debug mode is enabled");
  println("[INIT] Starting...");

  initDisplay();
  println("--------------");
  initCan();
  println("--------------");
  initServo();
  println("--------------");
  servoDiagnostics();

  println("[INIT] Initialization is complete");

  renderAllData();
}

void loop() {
  while (CAN_MSGAVAIL == CAN.checkReceive()) {
    CAN.readMsgBuf(&len, buf);
    canMessageProcessing(CAN.getCanId(), buf);
  }

  if (isDataUpdated) {
    isDataUpdated = false;
    openCloseShutters();
    renderAllData();
  }
}

// Open or close grille shutters
void openCloseShutters() {
  float temp = getEngineTemp();
  float speed = getSpeed();
  bool openShutters = true;

  if (temp <= 75) {
    openShutters = false;
  }

  if (speed > 130) {
    openShutters = (temp > 90);
  }

  print("[INFO] Shutters must be ");
  print(String(openShutters ? servoDegreeMin : servoDegreeMax));
  print(" ");
  print("(" + String(openShutters ? "open" : "close") + ")");
  println("");

  int degreeNeedle = openShutters ? servoDegreeMin : servoDegreeMax;
  if (!isServoRotated(degreeNeedle)) {
    writeServo(degreeNeedle);
  }
}

void renderAllData() {
  display.setTextSize(textSize);
  display.clearDisplay();

  renderEngineTemp();
  renderCarSpeed();
  renderProgressBar();

  display.display();
}

void renderEngineTemp() {
  display.setCursor(0, 0);
  //display.println(String(getEngineTemp(), 1) + " oC");
  display.println(String(getEngineTemp(), 1) + "|" + String(getEngineTemp2(), 0));
}

void renderCarSpeed() {
  display.setCursor(0, 16);
  //display.println(String(getSpeed(), 1) + " km/h");
  display.println(String(getSpeed(), 1) + "|" + String(getSpeed2(), 1));
}

void renderProgressBar() {
  int shutterDegrees = getShutterDegree();
  //String text = String(shutterDegrees);
  String text = String(getCvtfTemp(), 1);
  int progress = map(shutterDegrees, servoDegreeMin, servoDegreeMax, 0, progressBarLengthInner);
  int y = constrain(51, 0, SCREEN_HEIGHT);
  int x = (SCREEN_WIDTH - text.length() * DEFAULT_SYMBOL_WIDTH * progressBarTextSize) / 2;

  display.setTextSize(progressBarTextSize);
  display.setCursor(x, y - DEFAULT_SYMBOL_HEIGHT * progressBarTextSize);
  display.println(text);

  display.drawRect(
    progressBarMarginOuter,
    y,
    progressBarLengthOuter,
    progressBarHeightOuter,
    HIGH
  );
  display.fillRect(
    progressBarMarginInner,
    y + progressBarBorder,
    progress ? : progressBarLengthInner,
    progressBarHeightInner,
    progress ? HIGH : LOW
  );
  display.display();
}

float getCvtfTemp() {
  return cvtfTemp;
}

float getEngineTemp() {
  return engineTemp;
}

float getEngineTemp2() {
  return engineTemp2;
}

float getSpeed() {
  return carSpeed;
}

float getSpeed2() {
  return carSpeed2;
}

int getShutterDegree() {
  return shutterDegree;
}

// CAN message processing
void canMessageProcessing(unsigned long messageId, byte* messageData) {
  String id = String(messageId, HEX);

  // Engine temp 1
  if (id == "324") {
    float engineTempOld = getEngineTemp();

    engineTemp = messageData[0] - 40.0;

    if (engineTempOld != engineTemp) {
      isDataUpdated = true;

      println("EngineTemp: " + String(getEngineTemp()));
    }
  }
  // Engine temp 2
  else if (id == "396") {
    float engineTemp2Old = getEngineTemp2();

    engineTemp2 = (float) messageData[2];

    if (engineTemp2Old != engineTemp2) {
      isDataUpdated = true;

      println("EngineTemp2: " + String(getEngineTemp2()));
    }
  }
  // Speeds (general)
  else if (id == "158") {
    float carSpeedOld = getSpeed();
    float carSpeed2Old = getSpeed2();

    carSpeed = (messageData[0] * 256 + messageData[1]) / 100.0;
    carSpeed2 = (messageData[4] * 256 + messageData[5]) / 100.0;

    if (carSpeedOld != carSpeed || carSpeed2Old != carSpeed2) {
      isDataUpdated = true;

      println("Speed: " + String(getSpeed()));
      println("Speed2: " + String(getSpeed2()));
    }
  }
  // CVTF temp
  else if (id == "510") {
    float cvtfTempOld = getCvtfTemp();

    cvtfTemp = messageData[5] - 40.0;

    if (cvtfTempOld != cvtfTemp) {
      isDataUpdated = true;

      println("CvtfTemp: " + String(getCvtfTemp()));
    }
  }
}

// Returns analog degree for servo
int getAnalogDegree() {
  int analogVal = analogRead(pinServoAnalog);
  analogVal = constrain(analogVal, servoAnalogMin, servoAnalogMax);
  analogDegree = map(analogVal, servoAnalogMin, servoAnalogMax, servoDegreeMin, servoDegreeMax);

  return analogDegree;
}

// It returns the status of whether the servo turned
bool isServoRotated(int degreeNeedle) {
  bool rotated = false;

  // Check by analog value
  int analogVal = analogRead(pinServoAnalog);
  int checkMinAnalog = servoAnalogMin - servoAnalogAnalogDiff;
  int checkMaxAnalog = servoAnalogMax + servoAnalogAnalogDiff;
  rotated = analogVal > checkMinAnalog && analogVal < checkMaxAnalog;

  print("[INFO] Analog: ");
  print(String(analogVal));
  println(" | Diff min: " + String(checkMinAnalog) + " | Diff max: " + String(checkMaxAnalog));

  // Check by digital value
  if (rotated) {
    int degreeAnalog = getAnalogDegree();
    int checkMin = degreeNeedle - servoAnalogDegreesDiff;
    int checkMax = degreeNeedle + servoAnalogDegreesDiff;
    rotated = degreeAnalog > checkMin && degreeAnalog < checkMax;

    print("[INFO] Digital: ");
    print(String(degreeAnalog) + "/" + String(degreeNeedle) + " (Analog/Digital)");
    println(" | Diff min: " + String(checkMin) + " | Diff max: " + String(checkMax));
  }

  println(rotated ? "[OK] Servo is rotated!" : "[FAIL] Servo is not rotated!");

  display.println("Servo: " + String(analogVal) + "|" + String(degreeNeedle));
  display.display();

  return rotated;
}

// Rotate servo
bool writeServo(int degree, bool isDiagnostics) {
  int start = getAnalogDegree();
  int end = degree;
  int position;

  if (start > end) {
    for (position = start; position >= end; position--)
    {
      servo.write(position);
      delay(isDiagnostics ? servoDiagDelay : servoDelay);
    }
  } else {
    for (position = start; position <= end; position++)
    {
      servo.write(position);
      delay(isDiagnostics ? servoDiagDelay : servoDelay);
    }
  }

  delay(300);

  shutterDegree = constrain(getAnalogDegree(), servoDegreeMin, servoDegreeMax);

  return isServoRotated(degree);
}

// Display initialization
void initDisplay() {
  if (!display.begin(SSD1306_SWITCHCAPVCC, 0x3C)) {
    println("[FAIL] SSD1306 allocation failed");
    for (;;);
  }
  println("[OK] SSD1306 allocation successful");

  display.clearDisplay();
  display.setTextColor(HIGH, LOW);
  display.display();

  println("[INIT] Display initialized");
}

// CAN bus initialization
void initCan() {
  //pinMode(pinCanInt, INPUT);
  while (CAN_OK != CAN.begin(CAN_500KBPS, MCP_8MHz)) {
    println("[FAIL] CAN BUS module init fail");
    println("[FAIL] Init CAN BUS module again");
    delay(100);
  }
  //CAN.setMode(MODE_NORMAL);

  println("[INIT] CAN initialized");

  // Hardware filters
  CAN.init_Mask(0, 0, 0x158);
  CAN.init_Mask(1, 0, 0x510);
  CAN.init_Filt(0, 0, 0x158);
  CAN.init_Filt(1, 0, 0x324);
  CAN.init_Filt(2, 0, 0x396);
  CAN.init_Filt(3, 0, 0x510);

  println("[INIT] CAN filters added");
}

// Servo initialization
void initServo() {
  pinMode(pinServoAnalog, INPUT);

  servo.attach(
    pinServo,
    servoMinUs,
    servoMaxUs
  );

  if (servo.attached()) {
    println("[INIT] Servo attached");
  }

  writeServo(newDegree);
}

// Diagnostics for servo
void servoDiagnostics() {
  display.setCursor(0, 0);
  display.println("Servo diag: start");
  display.display();

  println("[INIT] Servo diagnostics: start");

  bool diagStatus = true;
  diagStatus = writeServo(servoDegreeMax, true);

  //display.println("Servo diag #1: " + String(diagStatus ? "OK" : "FAIL"));
  //display.display();

  print(diagStatus ? "[OK]" : "[FAIL]");
  println(" Servo diagnostics #1 (to " + String(servoDegreeMax) + "°)");

  if (diagStatus) {
    diagStatus = writeServo(servoDegreeMin, true);
  }

  //display.println("Servo diag #2: " + String(diagStatus ? "OK" : "FAIL"));
  //display.display();

  print(diagStatus ? "[OK]" : "[FAIL]");
  println(" Servo diagnostics #2 (to " + String(servoDegreeMin) + "°)");

  if (diagStatus) {
    diagStatus = writeServo(servoDegreeMax, true);
  }

  //display.println("Servo diag #3: " + String(diagStatus ? "OK" : "FAIL"));
  //display.display();

  print(diagStatus ? "[OK]" : "[FAIL]");
  println(" Servo diagnostics #3 (to " + String(servoDegreeMax) + "°)");

  if (diagStatus) {
    diagStatus = writeServo(servoDegreeMin, true);
  }

  //display.println("Servo diag #4: " + String(diagStatus ? "OK" : "FAIL"));
  //display.display();

  print(diagStatus ? "[OK]" : "[FAIL]");
  println(" Servo diagnostics #4 (to " + String(servoDegreeMin) + "°)");

  if (!diagStatus) {
    while (true) {
      if (millis() - timer >= 3000) {
        timer = millis();

        display.println("");
        display.println("Life Is Pain");
        display.println("Shit happens...");
        display.display();

        println("[FAIL] Servo diagnostics: Shit happens...");
      }
    }
  }

  display.println("");
  display.println("Success!");
  display.display();

  println("[INIT] Servo diagnostics: success");
}

// Print message to Serial
void print(String message) {
  if (DEBUG_MODE) {
    Serial.print(message);
  }
}

// Print message to Serial
void println(String message) {
  if (DEBUG_MODE) {
    Serial.println(message);
  }
}
